# Fritzing sketch RFTT (saved by Fritzing 0.9.2b)

parts:
  Part1 = Arduino Uno (Rev3)
  S1 = SWITCH-MOMENTARY-2 [package=tactile_switch_tall]  # not connected
  S2 = SWITCH-MOMENTARY-2 [package=tactile_switch_tall]  # not connected
  S3 = SWITCH-MOMENTARY-2 [package=tactile_switch_tall]  # not connected
  S4 = SWITCH-MOMENTARY-2 [package=tactile_switch_tall]  # not connected
  S5 = SWITCH-MOMENTARY-2 [package=tactile_switch_tall]  # not connected
  S6 = SWITCH-MOMENTARY-2 [package=tactile_switch_tall]  # not connected
  S7 = SWITCH-MOMENTARY-2 [package=tactile_switch_tall]  # not connected
  S8 = SWITCH-MOMENTARY-2 [package=tactile_switch_tall]  # not connected
  S9 = SWITCH-MOMENTARY-2 [package=tactile_switch_tall]  # not connected
  S10 = SWITCH-MOMENTARY-2 [package=tactile_switch_tall]  # not connected
  S11 = SWITCH-MOMENTARY-2 [package=tactile_switch_tall]  # not connected
  S12 = SWITCH-MOMENTARY-2 [package=tactile_switch_tall]  # not connected
  S13 = SWITCH-MOMENTARY-2 [package=tactile_switch_tall]  # not connected
  4x4_Keypad = SWITCH-MOMENTARY-2 [package=tactile_switch_tall]  # not connected
  S15 = SWITCH-MOMENTARY-2 [package=tactile_switch_tall]  # not connected
  S16 = SWITCH-MOMENTARY-2 [package=tactile_switch_tall]  # not connected
  JP2 = Header 8 [package=1x08_smd]
  BAT1 = Battery Holders [package=battcom_20mm_pth]  # not connected
  RTC_Module = DeadOn RTC - DS3234 Breakout
  OLED = Grove OLED 128x96
  nRF24L01 = MIRF [package=mirf]

nets:
  N1: Part1.A0, JP2.1
  N2: Part1.A1, JP2.2
  N3: Part1.A2, JP2.3
  N4: Part1.A3, JP2.4
  N5: Part1.A4/SDA, OLED.SCL
  N6: Part1.A5/SCL, OLED.SDA
  N7: Part1.D8, JP2.5
  N8: Part1.D9_PWM, nRF24L01.7
  N9: Part1.D10_PWM/SS, nRF24L01.6
  N10: Part1.D11_PWM/MOSI, nRF24L01.5
  N11: Part1.D12/MISO, nRF24L01.4
  N12: Part1.D13/SCK, nRF24L01.3
  N13: Part1.GND, nRF24L01.2
  N14: Part1.D2, RTC_Module.MOSI, RTC_Module.MISO
  N15: Part1.D3_PWM, RTC_Module.SCLK
  N16: Part1.D4, RTC_Module.INT/SQW
  N17: Part1.D5_PWM, JP2.8
  N18: Part1.D6_PWM, JP2.7
  N19: Part1.D7, JP2.6
